# Fritzing sketch Igelwaage (saved by Fritzing 0.9.9b)
circuit board: 6.8967cm x 5.6cm

parts:
  Reset = Momentary Switch [package=ksa_sealed_tac_switch]
  Boot = Momentary Switch [package=ksa_sealed_tac_switch]
  Setup = Momentary Switch [package=ksa_sealed_tac_switch]
  R1 = Resistor [tolerance=±5% power=0.25 resistance=10k package=THT]
  J1 = female pin header, 5 pins [form="♀ (female)"]
  HX711 = HX711 XFW Weighing Sensor Module
  ESP8266-07 = Gizwits WiFi Witty ESP-12F
  Load_Cell = Camdenboss CTB0158-4 [part_number=CTB0158-4 package=THT]
  3V = Camdenboss CTB0158-2 [part_number=3V package=THT]

nets:
  GND: Reset.1, Boot.1, R1.Pin_0, J1.pin4, HX711.GND, ESP8266-07.GND, 3V.pin2
  N1: Reset.4, ESP8266-07.REST, ESP8266-07.GPIO16
  N2: Boot.4, ESP8266-07.GPIO0
  N3: Setup.2, R1.Pin_1, ESP8266-07.GPIO13
  VCC: Setup.3, J1.pin1, HX711.VCC, ESP8266-07.CH_PD, ESP8266-07.VCC, 3V.pin1
  N4: J1.pin2, ESP8266-07.RXD
  N5: J1.pin3, ESP8266-07.TXD
  N6: HX711.DO/RX, ESP8266-07.GPIO14
  N7: HX711.CK/TX, ESP8266-07.GPIO12
  N8: HX711.E+, Load_Cell.pin4
  N9: HX711.E-, Load_Cell.pin3
  N10: HX711.A+, Load_Cell.pin2
  N11: HX711.A-, Load_Cell.pin1

notes:
  WiFi Scale
  +
  -
  Rev. 1.4
  3V
  TX
  RX
  G
  5V
  E+
  USB-TTL
  Power
  E-
  A+
  A-

custom parts:
  HX711 XFW Weighing Sensor Module: HX711 is a precision 24-bit analog-to-digital converter (ADC) designed for weigh scales and industrial control applications to interface directly with a bridge sensor. Innovateking-EU HX711 Loadcell sensor
  Gizwits WiFi Witty ESP-12F: A breadboard friendly two part WiFi development board by Gizwits, powered by an ESP8266 ESP-12F SoC, featuring twin micro-usb ports, a photoresistor, a WS2812 RGB-LED and three buttons. The board comes in two parts. The bottom half has reset and flash buttons, a micro-usb with CH340 UART and 2x 1x08 female headers. The top half has the ESP-12F, LDR, RGB-LED, micro-usb (for power only), an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
  Camdenboss CTB0158-4: Camdenboss CTB0158-4 5.08mm (0.2") Pitch Standard Profile 90 ̊ Rising Clamp Terminal, 4 pole The real-life connectors are modular, made up of two or three connector blocks slotted together. These can be further slotted together to make larger connectors. Fritzing part is derived from Screw terminals by Lionel Michel. Because of the offset between connection pins and screw terminals, these are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
  Camdenboss CTB0158-2: Camdenboss CTB0158-2 5.08mm (0.2") Pitch Standard Profile 90 ̊ Rising Clamp Terminal, 2 pole The real-life connectors are modular, made up of two or three connector blocks slotted together. These can be further slotted together to make larger connectors. Fritzing part is derived from Screw terminals by Lionel Michel. Because of the offset between connection pins and screw terminals, these are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
